// Logisim project logisim.circ as structural Verilog: 19 circuits, main circuit main
// Instruction Register
module main (
);

  wire ALU_2_carry, ALU_2_zero, and_1_out, and_2_out, button_1_out, Carry_out, clock_1_out, CU_increment_p,
       CU_ram_select_m, CU_reset_p1, CU_update_ram, demultiplexer_1_out0, demultiplexer_1_out1,
       demultiplexer_1_out2, demultiplexer_1_out3, demultiplexer_1_out4, demultiplexer_1_out5,
       demultiplexer_1_out6, demultiplexer_1_out7, demultiplexer_2_out0, demultiplexer_2_out1,
       demultiplexer_2_out4, demultiplexer_2_out5, demultiplexer_2_out6, demultiplexer_2_out7, not_1_out,
       Zero_out;
  wire [1:0] CU_update_ir;
  wire [2:0] CU_bus_input, CU_update_registers;
  wire [3:0] CU_alu;
  wire [7:0] A_output, ALU_2_bus, B_output, C_2_output, controlled_buffer_1_out, D_2_output, ram_1_data;
  wire [15:0] M1_output, multiplexer_1_out, Program_Counter_mem_out;

  Clock clock_1 (.out(clock_1_out));
  Button button_1 (.out(button_1_out));
  not not_1 (not_1_out, CU_update_ram);
  // Probe on Program_Counter_mem_out
  RAM #(.addrWidth(16), .bus("asynch")) ram_1 (
    .addr(multiplexer_1_out), .data(ram_1_data), .ld(not_1_out));  // open: sel, clr
  // Probe on M1_output
  Multiplexer #(.width(16), .enable("false")) multiplexer_1 (
    .in0(Program_Counter_mem_out), .in1(M1_output), .out(multiplexer_1_out), .sel(CU_ram_select_m));
  and and_1 (and_1_out, CU_update_ir[0], ~CU_update_ir[1]);  // AND_Gate
  Control_Unit CU (
    .Reset(button_1_out), .Clock(clock_1_out), .BUS_in(controlled_buffer_1_out), .Carry(Carry_out),
    .IsZero(Zero_out), .Increment_P(CU_increment_p), .Bus_Input(CU_bus_input),
    .Update_Registers(CU_update_registers), .Reset_P1(CU_reset_p1), .ALU(CU_alu), .Update_RAM(CU_update_ram),
    .RAM_select_M(CU_ram_select_m), .Update_IR(CU_update_ir));
  Program_Counter Program_Counter (
    .BUS_to_P2(demultiplexer_1_out7), .BUS_in(controlled_buffer_1_out), .Reset_P1(CU_reset_p1),
    .Increment(CU_increment_p), .Bus_to_P1(demultiplexer_1_out6), .Mem_Out(Program_Counter_mem_out));
  MemoryCell M2 (.Input(controlled_buffer_1_out), .Set(demultiplexer_1_out5), .Output(M1_output[15:8]));
  MemoryCell M1 (.Input(controlled_buffer_1_out), .Set(demultiplexer_1_out4), .Output(M1_output[7:0]));
  Demultiplexer #(.select(3), .disabled(0), .enable("false")) demultiplexer_1 (
    .out0(demultiplexer_1_out0), .out1(demultiplexer_1_out1), .out2(demultiplexer_1_out2),
    .out3(demultiplexer_1_out3), .out4(demultiplexer_1_out4), .out5(demultiplexer_1_out5),
    .out6(demultiplexer_1_out6), .out7(demultiplexer_1_out7), .in(and_2_out), .sel(CU_update_registers));
  and and_2 (and_2_out, clock_1_out, and_1_out);
  // Probe on CU_update_ir
  Demultiplexer #(.select(3), .disabled(0), .enable("false")) demultiplexer_2 (
    .out0(demultiplexer_2_out0), .out1(demultiplexer_2_out1), .out4(demultiplexer_2_out4),
    .out5(demultiplexer_2_out5), .out6(demultiplexer_2_out6), .out7(demultiplexer_2_out7), .in(1'b1),
    .sel(CU_bus_input));  // open: out2, out3
  // Probe on C_2_output
  assign controlled_buffer_1_out = demultiplexer_2_out6 ? C_2_output : 8'bz;  // Controlled_Buffer controlled_buffer_1
  MemoryCell C_2 (.Input(controlled_buffer_1_out), .Set(demultiplexer_1_out2), .Output(C_2_output));
  assign controlled_buffer_1_out = demultiplexer_2_out0 ? ram_1_data : 8'bz;  // Controlled_Buffer controlled_buffer_2
  assign ram_1_data = CU_update_ram ? controlled_buffer_1_out : 8'bz;  // Controlled_Buffer controlled_buffer_3
  // Probe on D_2_output
  MemoryCell D_2 (.Input(controlled_buffer_1_out), .Set(demultiplexer_1_out3), .Output(D_2_output));
  assign controlled_buffer_1_out = demultiplexer_2_out7 ? D_2_output : 8'bz;  // Controlled_Buffer controlled_buffer_4
  assign controlled_buffer_1_out = demultiplexer_2_out4 ? A_output : 8'bz;  // Controlled_Buffer controlled_buffer_5
  assign controlled_buffer_1_out = demultiplexer_2_out5 ? B_output : 8'bz;  // Controlled_Buffer controlled_buffer_6
  MemoryCell A (.Input(controlled_buffer_1_out), .Set(demultiplexer_1_out0), .Output(A_output));
  MemoryCell B (.Input(controlled_buffer_1_out), .Set(demultiplexer_1_out1), .Output(B_output));
  // Probe on controlled_buffer_1_out
  // Probe on A_output
  assign controlled_buffer_1_out = demultiplexer_2_out1 ? ALU_2_bus : 8'bz;  // Controlled_Buffer controlled_buffer_7
  // Probe on CU_alu
  ALU ALU_2 (
    .Control_Unit(CU_alu), .Carry(ALU_2_carry), .Zero(ALU_2_zero), .Bus(ALU_2_bus), .A(A_output), .B(B_output));
  // Probe on B_output
  MS_D_Latch Carry (.Input(ALU_2_carry), .Clock(clock_1_out), .Out(Carry_out));  // open: Inverted_Out
  MS_D_Latch Zero (.Input(ALU_2_zero), .Clock(clock_1_out), .Out(Zero_out));  // open: Inverted_Out
endmodule

module Control_Unit (
  input  Reset,
  input  Clock,
  input  [7:0] BUS_in,
  input  Carry,
  input  IsZero,
  output Increment_P,
  output [2:0] Bus_Input,
  output [2:0] Update_Registers,
  output Reset_P1,
  output [3:0] ALU,
  output Update_RAM,
  output RAM_select_M,
  output [1:0] Update_IR
);

  wire and_1_out, and_2_out, and_3_out, and_4_out, and_5_out, buffer_9_out, buffer_10_out, buffer_11_out,
       buffer_12_out, buffer_13_out, buffer_14_out, buffer_15_out, buffer_16_out, buffer_17_out,
       buffer_18_out, buffer_19_out, buffer_20_out, buffer_21_out, buffer_22_out, buffer_23_out,
       buffer_24_out, buffer_25_out, buffer_26_out, buffer_27_out, buffer_28_out, high_qn, low_qn,
       multiplexer_2_out, not_1_out, not_2_out;
  wire [1:0] low_2_q, low_q;
  wire [7:0] IR_output, multiplexer_1_out;
  wire [9:0] buffer_1_out, buffer_2_out, buffer_3_out, buffer_4_out, buffer_5_out, buffer_6_out,
       buffer_7_out, buffer_8_out;

  and and_1 (and_1_out, ~not_1_out, ~Clock);  // AND_Gate
  not not_1 (not_1_out, Clock);
  Multiplexer #(.width(8), .enable("false")) multiplexer_1 (
    .in0(BUS_in), .in1({8{1'b1}}), .out(multiplexer_1_out), .sel(Reset));
  D_Flip_Flop low (.clk(and_1_out), .D(low_qn), .Q(low_q[0]), .Qn(low_qn));  // open: preset, en, reset
  not not_2 (not_2_out, Clock);
  and and_2 (and_2_out, not_2_out, Clock);
  Multiplexer #(.select(2), .enable("false")) multiplexer_2 (
    .in0(and_3_out), .in1(and_3_out), .in2(Carry), .in3(IsZero), .out(multiplexer_2_out), .sel(low_2_q));
  D_Flip_Flop high (.clk(low_qn), .D(high_qn), .Q(low_q[1]), .Qn(high_qn));  // open: preset, en, reset
  and and_3 (and_3_out, low_qn, high_qn);
  and and_4 (and_4_out, and_2_out, multiplexer_2_out);
  // Probe on low_2_q
  MemoryCell IR (.Input(multiplexer_1_out), .Set(and_4_out), .Output(IR_output));
  // Probe on IR_output
  assign buffer_1_out = buffer_3_out;  // Buffer buffer_1, 10 bits wide
  assign buffer_2_out = buffer_1_out;  // Buffer buffer_2, 10 bits wide
  assign buffer_3_out = {IR_output, low_q};  // Buffer buffer_3, 10 bits wide
  assign buffer_4_out = buffer_5_out;  // Buffer buffer_4, 10 bits wide
  assign buffer_5_out = buffer_6_out;  // Buffer buffer_5, 10 bits wide
  assign buffer_6_out = buffer_7_out;  // Buffer buffer_6, 10 bits wide
  assign buffer_7_out = buffer_2_out;  // Buffer buffer_7, 10 bits wide
  and and_5 (and_5_out, buffer_27_out, buffer_11_out);
  assign buffer_8_out = buffer_4_out;  // Buffer buffer_8, 10 bits wide
  buf buffer_9 (buffer_9_out, buffer_12_out);
  buf buffer_10 (buffer_10_out, buffer_16_out);
  buf buffer_11 (buffer_11_out, buffer_9_out);
  buf buffer_12 (buffer_12_out, buffer_10_out);
  buf buffer_13 (buffer_13_out, buffer_15_out);
  buf buffer_14 (buffer_14_out, buffer_13_out);
  buf buffer_15 (buffer_15_out, Clock);
  buf buffer_16 (buffer_16_out, buffer_17_out);
  buf buffer_17 (buffer_17_out, buffer_18_out);
  buf buffer_18 (buffer_18_out, buffer_19_out);
  buf buffer_19 (buffer_19_out, buffer_25_out);
  buf buffer_20 (buffer_20_out, buffer_22_out);
  buf buffer_21 (buffer_21_out, buffer_23_out);
  buf buffer_22 (buffer_22_out, buffer_14_out);
  buf buffer_23 (buffer_23_out, buffer_20_out);
  ROM #(.addrWidth(10), .dataWidth(16)) rom_1 (
    .addr(buffer_8_out),
    .data({Update_IR, RAM_select_M, Update_RAM, ALU, Reset_P1, Update_Registers, Bus_Input, Increment_P}),
    .sel(and_5_out));
  D_Flip_Flop #(.trigger("falling")) high_2 (
    .clk(Clock), .D(Update_IR[1]), .Q(low_2_q[1]));  // open: Qn, preset, en, reset
  D_Flip_Flop #(.trigger("falling")) low_2 (
    .clk(Clock), .D(Update_IR[0]), .Q(low_2_q[0]));  // open: Qn, preset, en, reset
  buf buffer_24 (buffer_24_out, buffer_27_out);
  buf buffer_25 (buffer_25_out, buffer_24_out);
  buf buffer_26 (buffer_26_out, buffer_28_out);
  buf buffer_27 (buffer_27_out, buffer_26_out);
  buf buffer_28 (buffer_28_out, buffer_21_out);
  Pull_Resistor pull_resistor_1 (.node({Update_IR, RAM_select_M, Update_RAM, ALU, Reset_P1, Update_Registers, Bus_Input, Increment_P}));

  // Notes on the sheet:
  //   I don't know... fixes an error ^-^
  //   Update IR
  //   wait for IR to be updated
  //   contents of rom_1 (hex, n*v repeats v):
  //   0 0 0 1 0 0 4002 1 0 0 4012 1 0 0 4022 1 0 0 4032 1 0 0 3002 1 0 0 4042 1 0 0 4052 1 0 0 4102 1 0 0
  //   4112 1 0 0 4122 1 0 0 4132 1 0 0 3102 1 0 0 4142 1 0 0 4152 1 0 0 4202 1 0 0 4212 1 0 0 4222 1 0 0
  //   4232 1 0 0 3202 1 0 0 4242 1 0 0 4252 1 0 0 4302 1 0 0 4312 1 0 0 4322 1 0 0 4332 1 0 0 3302 1 0 0
  //   4342 1 0 0 4352 1 0 0 4402 1 0 0 4412 1 0 0 4422 1 0 0 4432 1 0 0 3402 1 0 0 4442 1 0 0 4452 1 0 0
  //   4f02 1 0 0 4f12 1 0 0 4f22 1 0 0 4f32 1 0 0 3f02 1 0 0 4f42 1 0 0 4f52 1 0 0 4602 1 0 0 4612 1 0 0
  //   4622 1 0 0 4632 1 0 0 3602 1 0 0 4642 1 0 0 4652 1 0 0 4502 1 0 0 4512 1 0 0 4522 1 0 0 4532 1 0 0
  //   3502 1 0 0 4542 1 0 0 4552 1 0 0 4018 1 0 0 4028 1 0 0 4038 1 0 0 3008 1 0 0 4048 1 0 0 4058 1 0 0
  //   400a 1 0 0 402a 1 0 0 403a 1 0 0 300a 1 0 0 404a 1 0 0 405a 1 0 0 400c 1 0 0 401c 1 0 0 403c 1 0 0
  //   300c 1 0 0 404c 1 0 0 405c 1 0 0 400e 1 0 0 401e 1 0 0 402e 1 0 0 300e 1 0 0 404e 1 0 0 405e 1 0 0
  //   6000 1 0 0 6010 1 0 0 6020 1 0 0 6030 1 0 0 6040 1 0 0 6050 1 0 1 4000 1 0 1 4010 1 0 1 4020 1 0 1
  //   4030 1 0 1 4040 1 0 1 4050 1 0 4402 4412 4403 11*0 4068 0 0 0 406a 0 0 0 406c 0 0 0 406e 0 0 0 6060
  //   0 0 1 4060 0 0 0 40f8 0 0 0 40fa 0 0 0 40fc 0 0 0 40fe 0 0 0 60f0 0 0 1 40f0 0 0 4078 406a 0 0 4078
  //   406c 0 0 4078 406e 0 0 4078 6060 0 1 4060 4078 0 0 407a 4068 0 0 407a 406c 0 0 407a 406e 0 0 407a
  //   6060 0 1 4060 407a 0 0 407c 4068 0 0 407c 406a 0 0 407c 406e 0 0 407c 6060 0 1 4060 407c 0 0 407e
  //   4068 0 0 407e 406a 0 0 407e 406c 0 0 407e 6060 0 1 4060 407e 0 0 6070 4068 0 0 6070 406a 0 0 6070
  //   406c 0 0 6070 406e 0 1 4060 6070 0 1 4070 4068 0 1 4070 406a 0 1 4070 406c 0 1 4070 406e 0 1 4070
  //   6060 216*0 c701 1 0 0 cf01 1 0 0 8201 1 0 0 8901 1 0 0 c101 1 0 0 c901 1 0 0 8a01 1 0 0 8101 1 0 0
  //   c701 1 1 0 cf01 1 1 0 8201 1 1 0 8901 1 1 0 c101 1 1 0 c901 1 1 0 8a01 1 1 0 8101 1 1
endmodule

module Program_Counter (
  input  BUS_to_P2,
  input  [7:0] BUS_in,
  input  Reset_P1,
  input  Increment,
  input  Bus_to_P1,
  output [15:0] Mem_Out
);

  wire and_1_out, and_2_out, and_3_out, and_4_out, and_5_out, and_6_out, and_7_out, and_8_out, and_9_out,
       halfadder_1_carry, halfadder_1_sum, halfadder_2_carry, halfadder_2_sum, halfadder_3_carry,
       halfadder_3_sum, halfadder_4_carry, halfadder_4_sum, halfadder_5_carry, halfadder_5_sum,
       halfadder_6_carry, halfadder_6_sum, halfadder_7_carry, halfadder_7_sum, halfadder_8_carry,
       halfadder_8_sum, halfadder_9_carry, halfadder_9_sum, halfadder_10_carry, halfadder_10_sum,
       halfadder_11_carry, halfadder_11_sum, halfadder_12_carry, halfadder_12_sum, halfadder_13_carry,
       halfadder_13_sum, halfadder_14_carry, halfadder_14_sum, halfadder_15_carry, halfadder_15_sum,
       multiplexer_1_out, multiplexer_2_out, multiplexer_3_out, multiplexer_4_out, multiplexer_5_out,
       multiplexer_6_out, multiplexer_7_out, multiplexer_8_out, multiplexer_9_out, multiplexer_10_out,
       multiplexer_11_out, multiplexer_12_out, multiplexer_13_out, multiplexer_14_out, multiplexer_15_out,
       multiplexer_16_out, not_1_out, or_1_out, or_2_out, xor_1_out;

  and and_1 (and_1_out, Increment, halfadder_15_carry);
  or or_1 (or_1_out, BUS_to_P2, Increment);
  Multiplexer #(.enable("false")) multiplexer_1 (
    .in0(BUS_in[0]), .in1(halfadder_1_sum), .out(multiplexer_1_out), .sel(Increment));
  not not_1 (not_1_out, Reset_P1);
  and and_2 (and_2_out, not_1_out, BUS_in[0]);
  Multiplexer #(.enable("false")) multiplexer_2 (
    .in0(and_2_out), .in1(halfadder_2_sum), .out(multiplexer_2_out), .sel(Increment));
  or or_2 (or_2_out, Increment, Reset_P1, Bus_to_P1);
  MS_D_Latch ms_d_latch_1 (.Input(multiplexer_1_out), .Clock(or_1_out), .Out(Mem_Out[8]));  // open: Inverted_Out
  HalfAdder halfadder_1 (.A(Mem_Out[8]), .B(and_1_out), .Sum(halfadder_1_sum), .Carry(halfadder_1_carry));
  and and_3 (and_3_out, not_1_out, BUS_in[1]);
  HalfAdder halfadder_2 (.A(Increment), .B(Mem_Out[0]), .Sum(halfadder_2_sum), .Carry(halfadder_2_carry));
  Multiplexer #(.enable("false")) multiplexer_3 (
    .in0(and_3_out), .in1(halfadder_4_sum), .out(multiplexer_3_out), .sel(Increment));
  MS_D_Latch ms_d_latch_2 (.Input(multiplexer_2_out), .Clock(or_2_out), .Out(Mem_Out[0]));  // open: Inverted_Out
  MS_D_Latch ms_d_latch_3 (.Input(multiplexer_4_out), .Clock(or_1_out), .Out(Mem_Out[9]));  // open: Inverted_Out
  Multiplexer #(.enable("false")) multiplexer_4 (
    .in0(BUS_in[1]), .in1(halfadder_3_sum), .out(multiplexer_4_out), .sel(Increment));
  HalfAdder halfadder_3 (.A(halfadder_1_carry), .B(Mem_Out[9]), .Sum(halfadder_3_sum), .Carry(halfadder_3_carry));
  and and_4 (and_4_out, not_1_out, BUS_in[2]);
  HalfAdder halfadder_4 (.A(halfadder_2_carry), .B(Mem_Out[1]), .Sum(halfadder_4_sum), .Carry(halfadder_4_carry));
  Multiplexer #(.enable("false")) multiplexer_5 (
    .in0(and_4_out), .in1(halfadder_6_sum), .out(multiplexer_5_out), .sel(Increment));
  MS_D_Latch ms_d_latch_4 (.Input(multiplexer_3_out), .Clock(or_2_out), .Out(Mem_Out[1]));  // open: Inverted_Out
  MS_D_Latch ms_d_latch_5 (.Input(multiplexer_6_out), .Clock(or_1_out), .Out(Mem_Out[10]));  // open: Inverted_Out
  Multiplexer #(.enable("false")) multiplexer_6 (
    .in0(BUS_in[2]), .in1(halfadder_5_sum), .out(multiplexer_6_out), .sel(Increment));
  HalfAdder halfadder_5 (.A(halfadder_3_carry), .B(Mem_Out[10]), .Sum(halfadder_5_sum), .Carry(halfadder_5_carry));
  and and_5 (and_5_out, not_1_out, BUS_in[3]);
  HalfAdder halfadder_6 (.A(halfadder_4_carry), .B(Mem_Out[2]), .Sum(halfadder_6_sum), .Carry(halfadder_6_carry));
  Multiplexer #(.enable("false")) multiplexer_7 (
    .in0(and_5_out), .in1(halfadder_8_sum), .out(multiplexer_7_out), .sel(Increment));
  MS_D_Latch ms_d_latch_6 (.Input(multiplexer_5_out), .Clock(or_2_out), .Out(Mem_Out[2]));  // open: Inverted_Out
  MS_D_Latch ms_d_latch_7 (.Input(multiplexer_8_out), .Clock(or_1_out), .Out(Mem_Out[11]));  // open: Inverted_Out
  Multiplexer #(.enable("false")) multiplexer_8 (
    .in0(BUS_in[3]), .in1(halfadder_7_sum), .out(multiplexer_8_out), .sel(Increment));
  HalfAdder halfadder_7 (.A(halfadder_5_carry), .B(Mem_Out[11]), .Sum(halfadder_7_sum), .Carry(halfadder_7_carry));
  and and_6 (and_6_out, not_1_out, BUS_in[4]);
  HalfAdder halfadder_8 (.A(halfadder_6_carry), .B(Mem_Out[3]), .Sum(halfadder_8_sum), .Carry(halfadder_8_carry));
  Multiplexer #(.enable("false")) multiplexer_9 (
    .in0(and_6_out), .in1(halfadder_10_sum), .out(multiplexer_9_out), .sel(Increment));
  MS_D_Latch ms_d_latch_8 (.Input(multiplexer_7_out), .Clock(or_2_out), .Out(Mem_Out[3]));  // open: Inverted_Out
  MS_D_Latch ms_d_latch_9 (.Input(multiplexer_10_out), .Clock(or_1_out), .Out(Mem_Out[12]));  // open: Inverted_Out
  Multiplexer #(.enable("false")) multiplexer_10 (
    .in0(BUS_in[4]), .in1(halfadder_9_sum), .out(multiplexer_10_out), .sel(Increment));
  HalfAdder halfadder_9 (.A(halfadder_7_carry), .B(Mem_Out[12]), .Sum(halfadder_9_sum), .Carry(halfadder_9_carry));
  and and_7 (and_7_out, not_1_out, BUS_in[5]);
  HalfAdder halfadder_10 (.A(halfadder_8_carry), .B(Mem_Out[4]), .Sum(halfadder_10_sum), .Carry(halfadder_10_carry));
  Multiplexer #(.enable("false")) multiplexer_11 (
    .in0(and_7_out), .in1(halfadder_12_sum), .out(multiplexer_11_out), .sel(Increment));
  MS_D_Latch ms_d_latch_10 (.Input(multiplexer_9_out), .Clock(or_2_out), .Out(Mem_Out[4]));  // open: Inverted_Out
  MS_D_Latch ms_d_latch_11 (.Input(multiplexer_12_out), .Clock(or_1_out), .Out(Mem_Out[13]));  // open: Inverted_Out
  Multiplexer #(.enable("false")) multiplexer_12 (
    .in0(BUS_in[5]), .in1(halfadder_11_sum), .out(multiplexer_12_out), .sel(Increment));
  HalfAdder halfadder_11 (.A(halfadder_9_carry), .B(Mem_Out[13]), .Sum(halfadder_11_sum), .Carry(halfadder_11_carry));
  and and_8 (and_8_out, not_1_out, BUS_in[6]);
  HalfAdder halfadder_12 (.A(halfadder_10_carry), .B(Mem_Out[5]), .Sum(halfadder_12_sum), .Carry(halfadder_12_carry));
  Multiplexer #(.enable("false")) multiplexer_13 (
    .in0(and_8_out), .in1(halfadder_14_sum), .out(multiplexer_13_out), .sel(Increment));
  MS_D_Latch ms_d_latch_12 (.Input(multiplexer_11_out), .Clock(or_2_out), .Out(Mem_Out[5]));  // open: Inverted_Out
  MS_D_Latch ms_d_latch_13 (.Input(multiplexer_14_out), .Clock(or_1_out), .Out(Mem_Out[14]));  // open: Inverted_Out
  Multiplexer #(.enable("false")) multiplexer_14 (
    .in0(BUS_in[6]), .in1(halfadder_13_sum), .out(multiplexer_14_out), .sel(Increment));
  HalfAdder halfadder_13 (.A(halfadder_11_carry), .B(Mem_Out[14]), .Sum(halfadder_13_sum), .Carry(halfadder_13_carry));
  and and_9 (and_9_out, not_1_out, BUS_in[7]);
  HalfAdder halfadder_14 (.A(halfadder_12_carry), .B(Mem_Out[6]), .Sum(halfadder_14_sum), .Carry(halfadder_14_carry));
  MS_D_Latch ms_d_latch_14 (.Input(multiplexer_13_out), .Clock(or_2_out), .Out(Mem_Out[6]));  // open: Inverted_Out
  MS_D_Latch ms_d_latch_15 (.Input(multiplexer_15_out), .Clock(or_1_out), .Out(Mem_Out[15]));  // open: Inverted_Out
  Multiplexer #(.enable("false")) multiplexer_15 (
    .in0(BUS_in[7]), .in1(xor_1_out), .out(multiplexer_15_out), .sel(Increment));
  xor xor_1 (xor_1_out, Mem_Out[15], halfadder_13_carry);
  HalfAdder halfadder_15 (.A(halfadder_14_carry), .B(Mem_Out[7]), .Sum(halfadder_15_sum), .Carry(halfadder_15_carry));
  Multiplexer #(.enable("false")) multiplexer_16 (
    .in0(and_9_out), .in1(halfadder_15_sum), .out(multiplexer_16_out), .sel(Increment));
  MS_D_Latch ms_d_latch_16 (.Input(multiplexer_16_out), .Clock(or_2_out), .Out(Mem_Out[7]));  // open: Inverted_Out
endmodule

module ALU (
  input  [7:0] A,
  input  [7:0] B,
  input  [3:0] Control_Unit,
  output Carry,
  output Zero,
  output [7:0] Bus
);

  wire Adder_carry, Cmp_zero_is_zero;
  wire [7:0] Adder_output, And_output_and, multiplexer_1_out, Or_output_or, shl_output_acc, shr_output_acc,
       Xor_output_xor;

  Adder Adder (
    .SubA(Control_Unit[1]), .SubB(Control_Unit[0]), .A(A), .B(B), .Output(Adder_output), .Carry(Adder_carry));
  And And (.Input_Acc(A), .Input_Bus(B), .Output_AND(And_output_and));
  Or Or (.Input_Acc(A), .Input_Bus(B), .Output_OR(Or_output_or));
  Xor Xor (.Input_Acc(A), .Input_Bus(B), .Output_XOR(Xor_output_xor));
  shl shl (.Input_Acc(A), .Output_Acc(shl_output_acc), .Input_Bus(B));
  shr shr (.Input_Acc(A), .Output_Acc(shr_output_acc), .Input_Bus(B));
  Multiplexer #(.select(3), .width(8), .enable("false")) multiplexer_1 (
    .in0(Adder_output), .in1(Adder_output), .in2(And_output_and), .in3(Or_output_or), .in4(Xor_output_xor),
    .in5(shl_output_acc), .in6(shr_output_acc), .in7(A), .out(multiplexer_1_out), .sel(Control_Unit[2:0]));
  xor xor_2 (Carry, Adder_carry, Control_Unit[3]);
  CmpZero Cmp_zero (.Input(multiplexer_1_out), .Is_Zero(Cmp_zero_is_zero));
  xor xor_3 (Zero, Cmp_zero_is_zero, Control_Unit[3]);
  Inverter Inverter (.Input(multiplexer_1_out), .Invert(Control_Unit[3]), .Output(Bus));
endmodule

module CmpZero (
  input  [7:0] Input,
  output Is_Zero
);

  wire or_1_out, or_2_out, or_3_out, or_4_out, or_5_out, or_6_out, or_7_out;

  or or_1 (or_1_out, Input[0], Input[1]);
  or or_2 (or_2_out, or_1_out, Input[2]);
  or or_3 (or_3_out, or_2_out, Input[3]);
  or or_4 (or_4_out, or_3_out, Input[4]);
  or or_5 (or_5_out, or_4_out, Input[5]);
  or or_6 (or_6_out, or_5_out, Input[6]);
  or or_7 (or_7_out, or_6_out, Input[7]);
  not not_1 (Is_Zero, or_7_out);
endmodule

module Inverter (
  input  [7:0] Input,
  input  Invert,
  output [7:0] Output
);

  wire [7:0] bit_extender_1_out;

  assign bit_extender_1_out = {{7{Invert}}, Invert};  // Bit_Extender bit_extender_1
  assign Output = Input ^ bit_extender_1_out;  // XOR_Gate xor_1, 8 bits wide
endmodule

module Adder (
  input  SubA,
  input  SubB,
  input  [7:0] A,
  input  [7:0] B,
  output [7:0] Output,
  output Carry
);

  wire fulladder_1_carry_out, fulladder_2_carry_out, fulladder_3_carry_out, fulladder_4_carry_out,
       fulladder_5_carry_out, fulladder_6_carry_out, fulladder_7_carry_out, fulladder_8_carry_out, xor_1_out,
       xor_2_out, xor_3_out, xor_4_out, xor_5_out, xor_6_out, xor_7_out, xor_8_out, xor_9_out, xor_10_out,
       xor_11_out, xor_12_out, xor_13_out, xor_14_out, xor_15_out, xor_16_out, xor_17_out, xor_18_out;

  xor xor_1 (xor_1_out, B[0], SubB);
  xor xor_2 (xor_2_out, B[1], SubB);
  xor xor_3 (xor_3_out, B[2], SubB);
  xor xor_4 (xor_4_out, B[3], SubB);
  xor xor_5 (xor_5_out, B[4], SubB);
  xor xor_6 (xor_6_out, B[5], SubB);
  xor xor_7 (xor_7_out, B[6], SubB);
  xor xor_8 (xor_8_out, B[7], SubB);
  xor xor_9 (xor_9_out, SubA, SubB);
  FullAdder fulladder_1 (
    .Carry_In(xor_9_out), .A(xor_10_out), .B(xor_1_out), .Sum(Output[0]), .Carry_Out(fulladder_1_carry_out));
  xor xor_10 (xor_10_out, SubA, A[0]);
  FullAdder fulladder_2 (
    .Carry_In(fulladder_1_carry_out), .A(xor_11_out), .B(xor_2_out), .Sum(Output[1]),
    .Carry_Out(fulladder_2_carry_out));
  xor xor_11 (xor_11_out, SubA, A[1]);
  FullAdder fulladder_3 (
    .Carry_In(fulladder_2_carry_out), .A(xor_12_out), .B(xor_3_out), .Sum(Output[2]),
    .Carry_Out(fulladder_3_carry_out));
  xor xor_12 (xor_12_out, SubA, A[2]);
  FullAdder fulladder_4 (
    .Carry_In(fulladder_3_carry_out), .A(xor_13_out), .B(xor_4_out), .Sum(Output[3]),
    .Carry_Out(fulladder_4_carry_out));
  xor xor_13 (xor_13_out, SubA, A[3]);
  FullAdder fulladder_5 (
    .Carry_In(fulladder_4_carry_out), .A(xor_14_out), .B(xor_5_out), .Sum(Output[4]),
    .Carry_Out(fulladder_5_carry_out));
  xor xor_14 (xor_14_out, SubA, A[4]);
  FullAdder fulladder_6 (
    .Carry_In(fulladder_5_carry_out), .A(xor_15_out), .B(xor_6_out), .Sum(Output[5]),
    .Carry_Out(fulladder_6_carry_out));
  xor xor_15 (xor_15_out, SubA, A[5]);
  FullAdder fulladder_7 (
    .Carry_In(fulladder_6_carry_out), .A(xor_16_out), .B(xor_7_out), .Sum(Output[6]),
    .Carry_Out(fulladder_7_carry_out));
  xor xor_16 (xor_16_out, SubA, A[6]);
  FullAdder fulladder_8 (
    .Carry_In(fulladder_7_carry_out), .A(xor_17_out), .B(xor_8_out), .Sum(Output[7]),
    .Carry_Out(fulladder_8_carry_out));
  xor xor_17 (xor_17_out, SubA, A[7]);
  xor xor_18 (xor_18_out, SubB, SubA);
  xor xor_19 (Carry, fulladder_8_carry_out, xor_18_out);
endmodule

module FullAdder (
  input  Carry_In,
  input  A,
  input  B,
  output Sum,
  output Carry_Out
);

  wire halfadder_1_carry, halfadder_1_sum, halfadder_2_carry;

  HalfAdder halfadder_1 (.A(A), .B(B), .Sum(halfadder_1_sum), .Carry(halfadder_1_carry));
  HalfAdder halfadder_2 (.A(Carry_In), .B(halfadder_1_sum), .Sum(Sum), .Carry(halfadder_2_carry));
  or or_1 (Carry_Out, halfadder_2_carry, halfadder_1_carry);
endmodule

module HalfAdder (
  input  A,
  input  B,
  output Sum,
  output Carry
);

  xor xor_1 (Sum, A, B);
  and and_1 (Carry, A, B);
endmodule

module And (
  input  [7:0] Input_Acc,
  input  [7:0] Input_Bus,
  output [7:0] Output_AND
);

  assign Output_AND = Input_Acc & Input_Bus;  // AND_Gate and_1, 8 bits wide
endmodule

module Or (
  input  [7:0] Input_Acc,
  input  [7:0] Input_Bus,
  output [7:0] Output_OR
);

  assign Output_OR = Input_Acc | Input_Bus;  // OR_Gate or_1, 8 bits wide
endmodule

module Xor (
  input  [7:0] Input_Acc,
  input  [7:0] Input_Bus,
  output [7:0] Output_XOR
);

  assign Output_XOR = Input_Acc ^ Input_Bus;  // XOR_Gate xor_1, 8 bits wide
endmodule

module shl (
  input  [7:0] Input_Acc,
  input  [7:0] Input_Bus,
  output [7:0] Output_Acc
);

  wire multiplexer_1_out, multiplexer_2_out, multiplexer_3_out, multiplexer_4_out, multiplexer_5_out,
       multiplexer_6_out, multiplexer_7_out, multiplexer_8_out, nor_1_out, or_1_out, or_2_out, or_3_out;

  Multiplexer #(.select(3), .enable("false")) multiplexer_1 (
    .in0(Input_Acc[0]), .in1(1'b0), .in2(1'b0), .in3(1'b0), .in4(1'b0), .in5(1'b0), .in6(1'b0), .in7(1'b0),
    .out(multiplexer_1_out), .sel(Input_Bus[2:0]));
  or or_1 (or_1_out, Input_Bus[3], Input_Bus[4]);
  Multiplexer #(.select(3), .enable("false")) multiplexer_2 (
    .in0(Input_Acc[2]), .in1(Input_Acc[1]), .in2(Input_Acc[0]), .in3(1'b0), .in4(1'b0), .in5(1'b0),
    .in6(1'b0), .in7(1'b0), .out(multiplexer_2_out), .sel(Input_Bus[2:0]));
  Multiplexer #(.select(3), .enable("false")) multiplexer_3 (
    .in0(Input_Acc[1]), .in1(Input_Acc[0]), .in2(1'b0), .in3(1'b0), .in4(1'b0), .in5(1'b0), .in6(1'b0),
    .in7(1'b0), .out(multiplexer_3_out), .sel(Input_Bus[2:0]));
  or or_2 (or_2_out, or_1_out, Input_Bus[5]);
  or or_3 (or_3_out, or_2_out, Input_Bus[6]);
  Multiplexer #(.select(3), .enable("false")) multiplexer_4 (
    .in0(Input_Acc[3]), .in1(Input_Acc[2]), .in2(Input_Acc[1]), .in3(Input_Acc[0]), .in4(1'b0), .in5(1'b0),
    .in6(1'b0), .in7(1'b0), .out(multiplexer_4_out), .sel(Input_Bus[2:0]));
  nor nor_1 (nor_1_out, or_3_out, Input_Bus[7]);
  Multiplexer #(.select(3), .enable("false")) multiplexer_5 (
    .in0(Input_Acc[4]), .in1(Input_Acc[3]), .in2(Input_Acc[2]), .in3(Input_Acc[1]), .in4(Input_Acc[0]),
    .in5(1'b0), .in6(1'b0), .in7(1'b0), .out(multiplexer_5_out), .sel(Input_Bus[2:0]));
  Multiplexer #(.select(3), .enable("false")) multiplexer_6 (
    .in0(Input_Acc[5]), .in1(Input_Acc[4]), .in2(Input_Acc[3]), .in3(Input_Acc[2]), .in4(Input_Acc[1]),
    .in5(Input_Acc[0]), .in6(1'b0), .in7(1'b0), .out(multiplexer_6_out), .sel(Input_Bus[2:0]));
  Multiplexer #(.select(3), .enable("false")) multiplexer_7 (
    .in0(Input_Acc[6]), .in1(Input_Acc[5]), .in2(Input_Acc[4]), .in3(Input_Acc[3]), .in4(Input_Acc[2]),
    .in5(Input_Acc[1]), .in6(Input_Acc[0]), .in7(1'b0), .out(multiplexer_7_out), .sel(Input_Bus[2:0]));
  Multiplexer #(.select(3), .enable("false")) multiplexer_8 (
    .in0(Input_Acc[7]), .in1(Input_Acc[6]), .in2(Input_Acc[5]), .in3(Input_Acc[4]), .in4(Input_Acc[3]),
    .in5(Input_Acc[2]), .in6(Input_Acc[1]), .in7(Input_Acc[0]), .out(multiplexer_8_out), .sel(Input_Bus[2:0]));
  and and_1 (Output_Acc[7], multiplexer_8_out, nor_1_out);
  and and_2 (Output_Acc[6], multiplexer_7_out, nor_1_out);
  and and_3 (Output_Acc[5], multiplexer_6_out, nor_1_out);
  and and_4 (Output_Acc[4], multiplexer_5_out, nor_1_out);
  and and_5 (Output_Acc[3], multiplexer_4_out, nor_1_out);
  and and_6 (Output_Acc[2], multiplexer_2_out, nor_1_out);
  and and_7 (Output_Acc[1], multiplexer_3_out, nor_1_out);
  and and_8 (Output_Acc[0], multiplexer_1_out, nor_1_out);
endmodule

module shr (
  input  [7:0] Input_Acc,
  input  [7:0] Input_Bus,
  output [7:0] Output_Acc
);

  wire multiplexer_1_out, multiplexer_2_out, multiplexer_3_out, multiplexer_4_out, multiplexer_5_out,
       multiplexer_6_out, multiplexer_7_out, multiplexer_8_out, nor_1_out, or_1_out, or_2_out, or_3_out;

  Multiplexer #(.select(3), .enable("false")) multiplexer_1 (
    .in0(Input_Acc[7]), .in1(1'b0), .in2(1'b0), .in3(1'b0), .in4(1'b0), .in5(1'b0), .in6(1'b0), .in7(1'b0),
    .out(multiplexer_1_out), .sel(Input_Bus[2:0]));
  or or_1 (or_1_out, Input_Bus[3], Input_Bus[4]);
  Multiplexer #(.select(3), .enable("false")) multiplexer_2 (
    .in0(Input_Acc[5]), .in1(Input_Acc[6]), .in2(Input_Acc[7]), .in3(1'b0), .in4(1'b0), .in5(1'b0),
    .in6(1'b0), .in7(1'b0), .out(multiplexer_2_out), .sel(Input_Bus[2:0]));
  Multiplexer #(.select(3), .enable("false")) multiplexer_3 (
    .in0(Input_Acc[6]), .in1(Input_Acc[7]), .in2(1'b0), .in3(1'b0), .in4(1'b0), .in5(1'b0), .in6(1'b0),
    .in7(1'b0), .out(multiplexer_3_out), .sel(Input_Bus[2:0]));
  or or_2 (or_2_out, or_1_out, Input_Bus[5]);
  or or_3 (or_3_out, or_2_out, Input_Bus[6]);
  Multiplexer #(.select(3), .enable("false")) multiplexer_4 (
    .in0(Input_Acc[4]), .in1(Input_Acc[5]), .in2(Input_Acc[6]), .in3(Input_Acc[7]), .in4(1'b0), .in5(1'b0),
    .in6(1'b0), .in7(1'b0), .out(multiplexer_4_out), .sel(Input_Bus[2:0]));
  nor nor_1 (nor_1_out, or_3_out, Input_Bus[7]);
  Multiplexer #(.select(3), .enable("false")) multiplexer_5 (
    .in0(Input_Acc[3]), .in1(Input_Acc[4]), .in2(Input_Acc[5]), .in3(Input_Acc[6]), .in4(Input_Acc[7]),
    .in5(1'b0), .in6(1'b0), .in7(1'b0), .out(multiplexer_5_out), .sel(Input_Bus[2:0]));
  Multiplexer #(.select(3), .enable("false")) multiplexer_6 (
    .in0(Input_Acc[2]), .in1(Input_Acc[3]), .in2(Input_Acc[4]), .in3(Input_Acc[5]), .in4(Input_Acc[6]),
    .in5(Input_Acc[7]), .in6(1'b0), .in7(1'b0), .out(multiplexer_6_out), .sel(Input_Bus[2:0]));
  Multiplexer #(.select(3), .enable("false")) multiplexer_7 (
    .in0(Input_Acc[1]), .in1(Input_Acc[2]), .in2(Input_Acc[3]), .in3(Input_Acc[4]), .in4(Input_Acc[5]),
    .in5(Input_Acc[6]), .in6(Input_Acc[7]), .in7(1'b0), .out(multiplexer_7_out), .sel(Input_Bus[2:0]));
  Multiplexer #(.select(3), .enable("false")) multiplexer_8 (
    .in0(Input_Acc[0]), .in1(Input_Acc[1]), .in2(Input_Acc[2]), .in3(Input_Acc[3]), .in4(Input_Acc[4]),
    .in5(Input_Acc[5]), .in6(Input_Acc[6]), .in7(Input_Acc[7]), .out(multiplexer_8_out), .sel(Input_Bus[2:0]));
  and and_1 (Output_Acc[0], multiplexer_8_out, nor_1_out);
  and and_2 (Output_Acc[1], multiplexer_7_out, nor_1_out);
  and and_3 (Output_Acc[2], multiplexer_6_out, nor_1_out);
  and and_4 (Output_Acc[3], multiplexer_5_out, nor_1_out);
  and and_5 (Output_Acc[4], multiplexer_4_out, nor_1_out);
  and and_6 (Output_Acc[5], multiplexer_2_out, nor_1_out);
  and and_7 (Output_Acc[6], multiplexer_3_out, nor_1_out);
  and and_8 (Output_Acc[7], multiplexer_1_out, nor_1_out);
endmodule

module RS_getaktet (
  input  Set,
  input  Clock,
  input  Reset,
  output Out,
  output Out_negate
);

  wire nand_1_out, nand_2_out;

  nand nand_1 (nand_1_out, Set, Clock);
  nand nand_2 (nand_2_out, Clock, Reset);
  nand nand_3 (Out, nand_1_out, Out_negate);
  nand nand_4 (Out_negate, Out, nand_2_out);
endmodule

module RS_ungetaktet (
  input  Out,
  input  R,
  input  S,
  input  Out_negate
);

  nor nor_1 (Out, Out_negate, R);
  nor nor_2 (Out_negate, S, Out);
endmodule

module MS_D_Latch (
  input  Input,
  input  Clock,
  output Out,
  output Inverted_Out
);

  D_Flip_Flop #(.trigger("falling")) d_ff_1 (
    .clk(Clock), .D(Input), .Q(Out), .Qn(Inverted_Out));  // open: preset, en, reset
endmodule

module MemoryCell (
  input  [7:0] Input,
  input  Set,
  output [7:0] Output
);

  MS_D_Latch ms_d_latch_1 (.Input(Input[0]), .Clock(Set), .Out(Output[0]));  // open: Inverted_Out
  MS_D_Latch ms_d_latch_2 (.Input(Input[1]), .Clock(Set), .Out(Output[1]));  // open: Inverted_Out
  MS_D_Latch ms_d_latch_3 (.Input(Input[2]), .Clock(Set), .Out(Output[2]));  // open: Inverted_Out
  MS_D_Latch ms_d_latch_4 (.Input(Input[3]), .Clock(Set), .Out(Output[3]));  // open: Inverted_Out
  MS_D_Latch ms_d_latch_5 (.Input(Input[4]), .Clock(Set), .Out(Output[4]));  // open: Inverted_Out
  MS_D_Latch ms_d_latch_6 (.Input(Input[5]), .Clock(Set), .Out(Output[5]));  // open: Inverted_Out
  MS_D_Latch ms_d_latch_7 (.Input(Input[6]), .Clock(Set), .Out(Output[6]));  // open: Inverted_Out
  MS_D_Latch ms_d_latch_8 (.Input(Input[7]), .Clock(Set), .Out(Output[7]));  // open: Inverted_Out
endmodule

module Tests (
  input  Sub,
  input  [7:0] A,
  input  [7:0] B,
  input  [7:0] in_4,
  input  [7:0] in_5,
  output [7:0] out_6,
  output [7:0] out_7,
  output out_8,
  output [7:0] out_9,
  output [7:0] out_10
);

  Or or_1 (.Input_Acc(in_5), .Input_Bus(in_4), .Output_OR(out_10));
  Inverter inverter_1 (.Input(8'hfe), .Output(out_6));  // open: Invert
  Adder adder_1 (.SubB(Sub), .A(A), .B(B), .Output(out_7), .Carry(out_8));  // open: SubA
  Xor xor_1 (.Input_Acc(in_4), .Input_Bus(in_5), .Output_XOR(out_9));
endmodule
