// Logisim project logisim74.circ as structural Verilog: 19 circuits, main circuit main
module main (
);

  wire ALU_garry, ALU_zero, button_1_out, clock_1_out, CU_don_t_increment_p, CU_don_t_reset_p1,
       CU_ram_select_m, CU_ram_select_pc, CU_update_ramsosse, CU_update_register, dip_7404_1_p2,
       dip_74138_1_p3, dip_74138_1_p5, dip_74138_1_p7, dip_74138_1_p9, dip_74138_1_p11, dip_74138_1_p13,
       dip_74138_1_p14, dip_74138_1_p15, dip_74138_2_p2, dip_74138_2_p4, dip_74138_2_p8, dip_74138_2_p10,
       dip_74138_2_p11, dip_74138_2_p12, Zero_Carry_p9, Zero_Carry_p10;
  wire [2:0] buffer_1_out, buffer_2_out, buffer_3_out, buffer_4_out, buffer_5_out, buffer_6_out,
       buffer_7_out, buffer_8_out, buffer_9_out, buffer_10_out, buffer_11_out, buffer_12_out, CU_bus_input,
       CU_update_reg;
  wire [3:0] CU_alu;
  wire [7:0] A_output, ALU_bus, B_output, C_output, CU_ir_value, D_output, M1_output, M2_output, PC_bus_out,
       PC_bus_out_2, ram_1_data, tri_state_buffer_6_output;
  wire [15:0] CU_microinstruction, tri_state_buffer_1_output;

  Clock clock_1 (.out(clock_1_out));
  Button button_1 (.out(button_1_out));
  // Probe on tri_state_buffer_1_output
  Tri_State_Buffer tri_state_buffer_1 (
    .Input(M1_output), .NotActive(CU_ram_select_m), .Output(tri_state_buffer_1_output[7:0]));
  Tri_State_Buffer tri_state_buffer_2 (
    .Input(M2_output), .NotActive(CU_ram_select_m), .Output(tri_state_buffer_1_output[15:8]));
  // Probe on CU_ir_value
  Tri_State_Buffer tri_state_buffer_3 (
    .Input(PC_bus_out), .NotActive(CU_ram_select_pc), .Output(tri_state_buffer_1_output[7:0]));
  Tri_State_Buffer tri_state_buffer_4 (
    .Input(PC_bus_out_2), .NotActive(CU_ram_select_pc), .Output(tri_state_buffer_1_output[15:8]));
  RAM #(.addrWidth(16), .bus("asynch")) ram_1 (
    .addr(tri_state_buffer_1_output), .data(ram_1_data), .ld(CU_update_ramsosse));  // open: sel, clr
  ControlUnit74 CU (
    .Clock(clock_1_out), .Reset(button_1_out), .Bus_in(tri_state_buffer_6_output), .Carry(Zero_Carry_p9),
    .isZero(Zero_Carry_p10), .IR_Value(CU_ir_value), .MicroInstruction(CU_microinstruction),
    .Don_t_Increment_P(CU_don_t_increment_p), .Bus_Input(CU_bus_input), .Update_Reg(CU_update_reg),
    .Don_t_Reset_P1(CU_don_t_reset_p1), .Alu(CU_alu), .Update_RAMSOSSE(CU_update_ramsosse),
    .RAM_select_M(CU_ram_select_m), .RAM_select_PC(CU_ram_select_pc), .Update_Register(CU_update_register));
  // Probe on CU_microinstruction
  PC74 PC (
    .P2(dip_74138_1_p14), .BUS_in(tri_state_buffer_6_output), .NotResetP1(CU_don_t_reset_p1),
    .P1(dip_74138_1_p15), .Bus_out({PC_bus_out_2, PC_bus_out}), .NotIncrement(CU_don_t_increment_p));
  Tri_State_Buffer tri_state_buffer_5 (
    .Input(tri_state_buffer_6_output), .NotActive(CU_update_ramsosse), .Output(ram_1_data));
  assign buffer_1_out = buffer_3_out;  // Buffer buffer_1, 3 bits wide
  assign buffer_2_out = buffer_1_out;  // Buffer buffer_2, 3 bits wide
  assign buffer_3_out = buffer_5_out;  // Buffer buffer_3, 3 bits wide
  assign buffer_4_out = buffer_2_out;  // Buffer buffer_4, 3 bits wide
  assign buffer_5_out = CU_update_reg;  // Buffer buffer_5, 3 bits wide
  assign buffer_6_out = buffer_4_out;  // Buffer buffer_6, 3 bits wide
  // Probe on CU_update_reg
  // Probe on {PC_bus_out_2, PC_bus_out}
  // DIP_74138 dip_74138_1: pin names not known; wires that end beside it: buffer_6_out, buffer_6_out[0], dip_74138_1_p3, buffer_6_out[1], dip_74138_1_p5, buffer_6_out[2], dip_74138_1_p7, 1'b0, dip_74138_1_p9, 1'b0, dip_74138_1_p11, CU_update_register, dip_74138_1_p13, dip_74138_1_p14, dip_74138_1_p15
  // Probe on {M2_output, M1_output}
  REGISTER74 M2 (.Input(tri_state_buffer_6_output), .RisingEdge(dip_74138_1_p13), .Output(M2_output));
  REGISTER74 M1 (.Input(tri_state_buffer_6_output), .RisingEdge(dip_74138_1_p11), .Output(M1_output));
  assign buffer_7_out = buffer_8_out;  // Buffer buffer_7, 3 bits wide
  assign buffer_8_out = buffer_9_out;  // Buffer buffer_8, 3 bits wide
  assign buffer_9_out = CU_bus_input;  // Buffer buffer_9, 3 bits wide
  assign buffer_10_out = buffer_7_out;  // Buffer buffer_10, 3 bits wide
  assign buffer_11_out = buffer_10_out;  // Buffer buffer_11, 3 bits wide
  assign buffer_12_out = buffer_11_out;  // Buffer buffer_12, 3 bits wide
  // Probe on buffer_12_out
  REGISTER74 C (.Input(tri_state_buffer_6_output), .RisingEdge(dip_74138_1_p7), .Output(C_output));
  Tri_State_Buffer tri_state_buffer_6 (
    .Input(ram_1_data), .NotActive(dip_74138_2_p2), .Output(tri_state_buffer_6_output));
  // Probe on dip_74138_2_p2
  // DIP_74138 dip_74138_2: pin names not known; wires that end beside it: buffer_12_out[0], dip_74138_2_p2, buffer_12_out[1], dip_74138_2_p4, buffer_12_out[2], 1'b0, 1'b0, dip_74138_2_p8, 1'b1, dip_74138_2_p10, dip_74138_2_p11, dip_74138_2_p12
  // Probe on C_output
  Tri_State_Buffer tri_state_buffer_7 (
    .Input(C_output), .NotActive(dip_74138_2_p12), .Output(tri_state_buffer_6_output));
  REGISTER74 D (.Input(tri_state_buffer_6_output), .RisingEdge(dip_74138_1_p9), .Output(D_output));
  // Probe on D_output
  Tri_State_Buffer tri_state_buffer_8 (
    .Input(D_output), .NotActive(dip_74138_2_p11), .Output(tri_state_buffer_6_output));
  REGISTER74 A (.Input(tri_state_buffer_6_output), .RisingEdge(dip_74138_1_p3), .Output(A_output));
  Tri_State_Buffer tri_state_buffer_9 (
    .Input(A_output), .NotActive(dip_74138_2_p8), .Output(tri_state_buffer_6_output));
  REGISTER74 B (.Input(tri_state_buffer_6_output), .RisingEdge(dip_74138_1_p5), .Output(B_output));
  Tri_State_Buffer tri_state_buffer_10 (
    .Input(B_output), .NotActive(dip_74138_2_p10), .Output(tri_state_buffer_6_output));
  Tri_State_Buffer tri_state_buffer_11 (
    .Input(ALU_bus), .NotActive(dip_74138_2_p4), .Output(tri_state_buffer_6_output));
  ALU74 ALU (.A(A_output), .B(B_output), .CU(CU_alu), .Zero(ALU_zero), .Bus(ALU_bus), .Garry(ALU_garry));
  // Probe on A_output
  // Probe on B_output
  // DIP_7404 dip_7404_1: pin names not known; wires that end beside it: clock_1_out, dip_7404_1_p2
  // DIP_7474 Zero_Carry: pin names not known; wires that end beside it: 1'b1, 1'b1, ALU_garry, 1'b1, dip_7404_1_p2, ALU_zero, 1'b1, dip_7404_1_p2, Zero_Carry_p9, Zero_Carry_p10
  // Probe on Zero_Carry_p10
  // Probe on Zero_Carry_p9
  // Probe on tri_state_buffer_6_output
  // Probe on CU_alu

  // Notes on the sheet:
  //   Bugfix Err3294: buffer to not set A
endmodule

module PC74 (
  input  P2,
  input  [7:0] BUS_in,
  input  NotResetP1,
  input  NotIncrement,
  input  P1,
  output [15:0] Bus_out
);

  wire AND_p3, AND_p6;
  wire [6:1] XOR_2_p2;
  wire [7:0] AND_2_p3, buffer_1_out, buffer_2_out, D_FF_2_p2, MUX_p4, XOR_p6;

  // DIP_7408 AND: pin names not known; wires that end beside it: NotResetP1, P1, AND_p3, AND_p3, NotIncrement, AND_p6
  // DIP_7486 XOR: pin names not known; wires that end beside it: Bus_out[7], 1'b1, XOR_2_p2[6], Bus_out[0], XOR_p6[7], XOR_p6[0], Bus_out[6], Bus_out[0], XOR_2_p2[5], Bus_out[1], XOR_p6[6], XOR_p6[1]
  // DIP_7474 D_FF: pin names not known; wires that end beside it: 1'b1, BUS_in[0], P2, 1'b1, Bus_out[8], 1'b1, 1'b1, BUS_in[1], P2, Bus_out[9]
  // DIP_7408 AND_2: pin names not known; wires that end beside it: BUS_in[0], NotResetP1, AND_2_p3[0], BUS_in[1], NotResetP1, AND_2_p3[1], BUS_in[3], NotResetP1, AND_2_p3[3], BUS_in[2], NotResetP1, AND_2_p3[2]
  // DIP_7474 D_FF_2: pin names not known; wires that end beside it: 1'b1, D_FF_2_p2[0], AND_p6, 1'b1, Bus_out[0], 1'b1, 1'b1, D_FF_2_p2[1], AND_p6, Bus_out[1]
  // DIP_7486 XOR_2: pin names not known; wires that end beside it: Bus_out[5], XOR_2_p2[1], XOR_2_p2[4], Bus_out[2], XOR_p6[5], XOR_p6[2], Bus_out[4], XOR_2_p2[2], XOR_2_p2[3], Bus_out[3], XOR_p6[4], XOR_p6[3]
  // DIP_7408 AND_3: pin names not known; wires that end beside it: Bus_out[7], XOR_2_p2[6], Bus_out[6], Bus_out[1], XOR_2_p2[5], Bus_out[0], XOR_2_p2[6], XOR_2_p2[1]
  // DIP_7474 D_FF_3: pin names not known; wires that end beside it: 1'b1, D_FF_2_p2[2], AND_p6, 1'b1, Bus_out[2], 1'b1, D_FF_2_p2[3], AND_p6, Bus_out[3]
  // DIP_7474 D_FF_4: pin names not known; wires that end beside it: 1'b1, BUS_in[2], P2, 1'b1, Bus_out[10], 1'b1, 1'b1, BUS_in[3], P2, Bus_out[11]
  // DIP_7408 AND_4: pin names not known; wires that end beside it: BUS_in[4], NotResetP1, AND_2_p3[4], BUS_in[5], NotResetP1, AND_2_p3[5], BUS_in[7], NotResetP1, AND_2_p3[7], BUS_in[6], NotResetP1, AND_2_p3[6]
  // DIP_7474 D_FF_5: pin names not known; wires that end beside it: 1'b1, BUS_in[4], P2, 1'b1, Bus_out[12], 1'b1, 1'b1, BUS_in[5], P2, Bus_out[13]
  // DIP_7408 AND_5: pin names not known; wires that end beside it: Bus_out[5], Bus_out[2], XOR_2_p2[4], XOR_2_p2[1], XOR_2_p2[5], XOR_2_p2[2], Bus_out[4], Bus_out[3], XOR_2_p2[3], XOR_2_p2[2], XOR_2_p2[4], XOR_2_p2[3]
  // DIP_7474 D_FF_6: pin names not known; wires that end beside it: 1'b1, D_FF_2_p2[4], AND_p6, 1'b1, Bus_out[4], 1'b1, 1'b1, D_FF_2_p2[5], AND_p6, Bus_out[5]
  // DIP_7474 D_FF_7: pin names not known; wires that end beside it: 1'b1, D_FF_2_p2[6], AND_p6, 1'b1, Bus_out[6], 1'b1, 1'b1, D_FF_2_p2[7], AND_p6, Bus_out[7]
  // DIP_7474 D_FF_8: pin names not known; wires that end beside it: 1'b1, BUS_in[6], P2, 1'b1, Bus_out[14], 1'b1, 1'b1, BUS_in[7], P2, Bus_out[15]
  // DIP_74157 MUX: pin names not known; wires that end beside it: NotIncrement, XOR_p6[0], AND_2_p3[0], MUX_p4[0], XOR_p6[1], 1'b0, XOR_p6[7], AND_2_p3[7], MUX_p4[7]
  // DIP_74157 MUX_2: pin names not known; wires that end beside it: AND_2_p3[1], MUX_p4[1], NotIncrement, XOR_p6[2], AND_2_p3[2], MUX_p4[2], XOR_p6[3], AND_2_p3[3], MUX_p4[3], XOR_p6[6], AND_2_p3[6], MUX_p4[6], 1'b0, XOR_p6[5], AND_2_p3[5], MUX_p4[5], XOR_p6[4], AND_2_p3[4], MUX_p4[4]
  assign buffer_1_out = MUX_p4;  // Buffer buffer_1, 8 bits wide
  assign buffer_2_out = buffer_1_out;  // Buffer buffer_2, 8 bits wide
  assign D_FF_2_p2 = buffer_2_out;  // Buffer buffer_3, 8 bits wide
endmodule

module ALU74 (
  input  [7:0] A,
  input  [7:0] B,
  input  [3:0] CU,
  output Garry,
  output Zero,
  output [7:0] Bus
);

  wire ADD_carry, CMPZERO_is_zero;
  wire [7:0] ADD_summe, AND_out_3, mux_1_output_accu, OR_out_3, SHL_output_acc, SHR_output_acc, XOR_out_3;

  ADD74 ADD (.SUB_A(CU[1]), .B(B), .SUMME(ADD_summe), .CARRY(ADD_carry), .A(A), .SUB_B(CU[0]));
  AND74 AND (.A(A), .B(B), .out_3(AND_out_3));
  OR74 OR (.A(A), .B(B), .out_3(OR_out_3));
  XOR74 XOR (.A(A), .B(B), .out_3(XOR_out_3));
  SHL74 SHL (.B(B), .A(A), .Output_Acc(SHL_output_acc));
  SHR74 SHR (.B(B), .A(A), .Output_Acc(SHR_output_acc));
  MUX mux_1 (
    .ADD(ADD_summe), .SUB(ADD_summe), .AND(AND_out_3), .OR(OR_out_3), .XOR(XOR_out_3), .SHL(SHL_output_acc),
    .SHR(SHR_output_acc), .A(A), .Output_Accu(mux_1_output_accu), .CU(CU[2:0]));
  // Probe on SHR_output_acc
  // Probe on SHL_output_acc
  // Probe on XOR_out_3
  // Probe on OR_out_3
  // Probe on AND_out_3
  // Probe on ADD_summe
  CMPZERO74 CMPZERO (.Input(mux_1_output_accu), .is_zero(CMPZERO_is_zero));
  // DIP_7486 XOR_3: pin names not known; wires that end beside it: CMPZERO_is_zero, CU[3], CU[3], ADD_carry, Zero, Garry
  INV74 INV (.Input(mux_1_output_accu), .Output(Bus), .INV(CU[3]));
  // Probe on mux_1_output_accu
endmodule

module ControlUnit74 (
  input  Clock,
  input  Reset,
  input  [7:0] Bus_in,
  input  Carry,
  input  isZero,
  output Don_t_Increment_P,
  output [2:0] Bus_Input,
  output [2:0] Update_Reg,
  output Don_t_Reset_P1,
  output [3:0] Alu,
  output Update_RAMSOSSE,
  output RAM_select_M,
  output RAM_select_PC,
  output Update_Register,
  output [7:0] IR_Value,
  output [15:0] MicroInstruction
);

  wire AND_2_p3, AND_2_p4, AND_2_p5, AND_2_p6, AND_p4, AND_p6, AND_p8, buffer_2_out, buffer_3_out,
       buffer_4_out, buffer_5_out, buffer_7_out, buffer_8_out, buffer_9_out, buffer_10_out, buffer_11_out,
       buffer_12_out, buffer_13_out, buffer_14_out, buffer_15_out, buffer_16_out, buffer_17_out,
       buffer_18_out, buffer_19_out, buffer_21_out, INCR_p2, INCR_p3, INCR_p9, mux_p1, mux_p2, mux_p6,
       mux_p8, not_1_out;
  wire [1:0] INCR_p5;
  wire [7:0] D_2_p14;

  // DIP_7474 INCR: pin names not known; wires that end beside it: 1'b1, INCR_p2, INCR_p3, 1'b1, INCR_p5[0], INCR_p2, 1'b1, 1'b1, INCR_p9, INCR_p2, INCR_p5[1], INCR_p9
  // DIP_74157 D: pin names not known; wires that end beside it: Reset, Bus_in[6], 1'b1, D_2_p14[6], Bus_in[7], 1'b1, D_2_p14[7], 1'b0, Bus_in[5], 1'b1, D_2_p14[5], Bus_in[4], 1'b1, D_2_p14[4]
  // DIP_74153 mux: pin names not known; wires that end beside it: mux_p1, mux_p2, mux_p2, Carry, isZero, mux_p6, 1'b0, mux_p8, 1'b0
  // DIP_7408 AND: pin names not known; wires that end beside it: INCR_p9, INCR_p2, mux_p2, AND_p4, MicroInstruction[14], AND_p6, AND_p6, AND_p8, Update_Register
  buf buffer_1 (AND_p8, buffer_3_out);
  // DIP_7408 AND_2: pin names not known; wires that end beside it: mux_p1, Clock, AND_2_p3, AND_2_p4, AND_2_p5, AND_2_p6
  buf buffer_2 (buffer_2_out, AND_p6);
  buf buffer_3 (buffer_3_out, buffer_2_out);
  // DIP_74157 D_2: pin names not known; wires that end beside it: Reset, Bus_in[2], 1'b1, D_2_p14[2], Bus_in[3], 1'b1, D_2_p14[3], 1'b0, Bus_in[1], 1'b1, D_2_p14[1], Bus_in[0], 1'b1, D_2_p14[0]
  REGISTER74 IR (.Input(D_2_p14), .RisingEdge(AND_2_p3), .Output(IR_Value));
  not not_1 (not_1_out, AND_2_p6);
  // DIP_7474 High_Low: pin names not known; wires that end beside it: 1'b1, 1'b1, MicroInstruction[15], 1'b1, not_1_out, MicroInstruction[14], 1'b1, not_1_out, mux_p6, mux_p8
  buf buffer_4 (buffer_4_out, buffer_5_out);
  buf buffer_5 (buffer_5_out, buffer_10_out);
  buf buffer_6 (AND_2_p5, buffer_4_out);
  buf buffer_7 (buffer_7_out, buffer_8_out);
  buf buffer_8 (buffer_8_out, Clock);
  buf buffer_9 (buffer_9_out, buffer_11_out);
  buf buffer_10 (buffer_10_out, buffer_12_out);
  buf buffer_11 (buffer_11_out, buffer_17_out);
  buf buffer_12 (buffer_12_out, buffer_9_out);
  buf buffer_13 (buffer_13_out, buffer_15_out);
  buf buffer_14 (buffer_14_out, buffer_7_out);
  buf buffer_15 (buffer_15_out, buffer_14_out);
  buf buffer_16 (buffer_16_out, buffer_13_out);
  buf buffer_17 (buffer_17_out, buffer_18_out);
  buf buffer_18 (buffer_18_out, AND_2_p4);
  buf buffer_19 (buffer_19_out, buffer_16_out);
  buf buffer_20 (AND_2_p4, buffer_21_out);
  buf buffer_21 (buffer_21_out, buffer_19_out);
  Pull_Resistor pull_resistor_1 (.node({MicroInstruction[15:12], Alu, MicroInstruction[7:4], Bus_Input, MicroInstruction[0]}));
  ROM #(.addrWidth(10), .dataWidth(16)) rom_1 (
    .addr({IR_Value, INCR_p5}),
    .data({MicroInstruction[15:12], Alu, MicroInstruction[7:4], Bus_Input, MicroInstruction[0]}),
    .sel(AND_2_p6));
  // DIP_7404 dip_7404_1: pin names not known; wires that end beside it: MicroInstruction[7], MicroInstruction[15], Don_t_Reset_P1, AND_p4, MicroInstruction[12], Clock, Update_RAMSOSSE, INCR_p3, MicroInstruction[0], MicroInstruction[13], Don_t_Increment_P, RAM_select_M

  assign {MicroInstruction[11:8], MicroInstruction[3:1]} = {Alu, Bus_Input};
  assign RAM_select_PC = MicroInstruction[13];
  assign Update_Reg = MicroInstruction[6:4];

  // Notes on the sheet:
  //   contents of rom_1 (hex, n*v repeats v):
  //   0 0 0 1 0 0 4002 1 0 0 4012 1 0 0 4022 1 0 0 4032 1 0 0 3002 1 0 0 4042 1 0 0 4052 1 0 0 4102 1 0 0
  //   4112 1 0 0 4122 1 0 0 4132 1 0 0 3102 1 0 0 4142 1 0 0 4152 1 0 0 4202 1 0 0 4212 1 0 0 4222 1 0 0
  //   4232 1 0 0 3202 1 0 0 4242 1 0 0 4252 1 0 0 4302 1 0 0 4312 1 0 0 4322 1 0 0 4332 1 0 0 3302 1 0 0
  //   4342 1 0 0 4352 1 0 0 4402 1 0 0 4412 1 0 0 4422 1 0 0 4432 1 0 0 3402 1 0 0 4442 1 0 0 4452 1 0 0
  //   4f02 1 0 0 4f12 1 0 0 4f22 1 0 0 4f32 1 0 0 3f02 1 0 0 4f42 1 0 0 4f52 1 0 0 4602 1 0 0 4612 1 0 0
  //   4622 1 0 0 4632 1 0 0 3602 1 0 0 4642 1 0 0 4652 1 0 0 4502 1 0 0 4512 1 0 0 4522 1 0 0 4532 1 0 0
  //   3502 1 0 0 4542 1 0 0 4552 1 0 0 4018 1 0 0 4028 1 0 0 4038 1 0 0 3008 1 0 0 4048 1 0 0 4058 1 0 0
  //   400a 1 0 0 402a 1 0 0 403a 1 0 0 300a 1 0 0 404a 1 0 0 405a 1 0 0 400c 1 0 0 401c 1 0 0 403c 1 0 0
  //   300c 1 0 0 404c 1 0 0 405c 1 0 0 400e 1 0 0 401e 1 0 0 402e 1 0 0 300e 1 0 0 404e 1 0 0 405e 1 0 0
  //   6000 1 0 0 6010 1 0 0 6020 1 0 0 6030 1 0 0 6040 1 0 0 6050 1 0 1 4000 1 0 1 4010 1 0 1 4020 1 0 1
  //   4030 1 0 1 4040 1 0 1 4050 1 0 4402 4412 4403 11*0 4068 0 0 0 406a 0 0 0 406c 0 0 0 406e 0 0 0 6060
  //   0 0 1 4060 0 0 0 40f8 0 0 0 40fa 0 0 0 40fc 0 0 0 40fe 0 0 0 60f0 0 0 1 40f0 0 0 4078 406a 0 0 4078
  //   406c 0 0 4078 406e 0 0 4078 6060 0 1 4060 4078 0 0 407a 4068 0 0 407a 406c 0 0 407a 406e 0 0 407a
  //   6060 0 1 4060 407a 0 0 407c 4068 0 0 407c 406a 0 0 407c 406e 0 0 407c 6060 0 1 4060 407c 0 0 407e
  //   4068 0 0 407e 406a 0 0 407e 406c 0 0 407e 6060 0 1 4060 407e 0 0 6070 4068 0 0 6070 406a 0 0 6070
  //   406c 0 0 6070 406e 0 1 4060 6070 0 1 4070 4068 0 1 4070 406a 0 1 4070 406c 0 1 4070 406e 0 1 4070
  //   6060 216*0 c701 1 0 0 cf01 1 0 0 8201 1 0 0 8901 1 0 0 c101 1 0 0 c901 1 0 0 8a01 1 0 0 8101 1 0 0
  //   c701 1 1 0 cf01 1 1 0 8201 1 1 0 8901 1 1 0 c101 1 1 0 c901 1 1 0 8a01 1 1 0 8101 1 1
endmodule

// Reg
module REGISTER74 (
  input  [7:0] Input,
  input  RisingEdge,
  output [7:0] Output
);

  // DIP_7474 dip_7474_1: pin names not known; wires that end beside it: 1'b1, Input[7], RisingEdge, 1'b1, Output[7], 1'b1, 1'b1, Input[0], RisingEdge
  // DIP_7474 dip_7474_2: pin names not known; wires that end beside it: 1'b1, Input[6], RisingEdge, 1'b1, Output[6], Output[0], 1'b1, 1'b1, Input[1], RisingEdge
  // DIP_7474 dip_7474_3: pin names not known; wires that end beside it: 1'b1, Input[5], RisingEdge, 1'b1, Output[5], Output[1], 1'b1, 1'b1, Input[2], RisingEdge
  // DIP_7474 dip_7474_4: pin names not known; wires that end beside it: 1'b1, Input[4], RisingEdge, 1'b1, Output[4], Output[2], 1'b1, 1'b1, Input[3], RisingEdge, Output[3]
endmodule

module AND74 (
  input  [7:0] A,
  input  [7:0] B,
  output [7:0] out_3
);

  // DIP_7408 dip_7408_1: pin names not known; wires that end beside it: B[7], B[3], A[7], A[3], out_3[7], out_3[3], B[6], B[2], A[6]
  // DIP_7408 dip_7408_2: pin names not known; wires that end beside it: A[2], out_3[6], out_3[2], B[5], B[1], A[5], A[1], out_3[5], out_3[1], B[4], B[0], A[4], A[0], out_3[4], out_3[0]
endmodule

module OR74 (
  input  [7:0] A,
  input  [7:0] B,
  output [7:0] out_3
);

  // DIP_7432 dip_7432_1: pin names not known; wires that end beside it: B[7], B[3], A[7], A[3], out_3[7], out_3[3], B[6], B[2], A[6]
  // DIP_7432 dip_7432_2: pin names not known; wires that end beside it: A[2], out_3[6], out_3[2], B[5], B[1], A[5], A[1], out_3[5], out_3[1], B[4], B[0], A[4], A[0], out_3[4], out_3[0]
endmodule

module XOR74 (
  input  [7:0] A,
  input  [7:0] B,
  output [7:0] out_3
);

  // DIP_7486 dip_7486_1: pin names not known; wires that end beside it: B[7], B[3], A[7], A[3], out_3[7], out_3[3], B[6], B[2], A[6]
  // DIP_7486 dip_7486_2: pin names not known; wires that end beside it: A[2], out_3[6], out_3[2], B[5], B[1], A[5], A[1], out_3[5], out_3[1], B[4], B[0], A[4], A[0], out_3[4], out_3[0]
endmodule

module ADD74 (
  input  SUB_A,
  input  SUB_B,
  input  [7:0] A,
  input  [7:0] B,
  output [7:0] SUMME,
  output CARRY
);

  wire dip_7486_9_p5, dip_7486_10_p7;
  wire [7:0] dip_7408_4_p14, dip_7408_4_p15, dip_7486_1_p5, dip_7486_4_p15, dip_7486_6_p14, dip_7486_8_p11;

  // DIP_7486 dip_7486_1: pin names not known; wires that end beside it: A[0], SUB_B, SUB_A, B[7], dip_7486_1_p5[0], dip_7486_4_p15[7], A[1], SUB_B, SUB_A
  // DIP_7486 dip_7486_2: pin names not known; wires that end beside it: B[6], dip_7486_1_p5[1], dip_7486_4_p15[6], A[2], SUB_B, SUB_A, B[5], dip_7486_1_p5[2], dip_7486_4_p15[5], A[3], SUB_B, SUB_A
  // DIP_7486 dip_7486_3: pin names not known; wires that end beside it: B[4], dip_7486_1_p5[3], dip_7486_4_p15[4], A[4], SUB_B, SUB_A, B[3], dip_7486_1_p5[4], dip_7486_4_p15[3], A[5], SUB_B, SUB_A
  // DIP_7486 dip_7486_4: pin names not known; wires that end beside it: B[2], dip_7486_1_p5[5], dip_7486_4_p15[2], A[6], SUB_B, SUB_A, B[1], dip_7486_1_p5[6], dip_7486_4_p15[1], SUB_A, SUB_B, A[7], B[0], dip_7486_1_p5[7], dip_7486_4_p15[0]
  // DIP_7486 dip_7486_5: pin names not known; wires that end beside it: dip_7486_1_p5[3], dip_7486_1_p5[4], dip_7486_4_p15[3], dip_7486_4_p15[4], dip_7486_6_p14[3], dip_7486_6_p14[4], dip_7486_1_p5[2], dip_7486_1_p5[5], dip_7486_4_p15[2]
  // DIP_7486 dip_7486_6: pin names not known; wires that end beside it: dip_7486_4_p15[5], dip_7486_6_p14[2], dip_7486_6_p14[5], dip_7486_1_p5[1], dip_7486_1_p5[6], dip_7486_4_p15[1], dip_7486_4_p15[6], dip_7486_6_p14[1], dip_7486_6_p14[6], dip_7486_1_p5[0], dip_7486_1_p5[7], dip_7486_4_p15[0], dip_7486_4_p15[7], dip_7486_6_p14[0], dip_7486_6_p14[7]
  // DIP_7408 dip_7408_1: pin names not known; wires that end beside it: dip_7486_8_p11[7], dip_7486_1_p5[7], dip_7486_6_p14[7], dip_7486_4_p15[7], dip_7408_4_p14[7], dip_7408_4_p15[7], dip_7486_8_p11[6], dip_7486_1_p5[6], dip_7486_6_p14[6]
  // DIP_7408 dip_7408_2: pin names not known; wires that end beside it: dip_7486_4_p15[6], dip_7408_4_p14[6], dip_7408_4_p15[6], dip_7486_8_p11[5], dip_7486_1_p5[5], dip_7486_6_p14[5], dip_7486_4_p15[5], dip_7408_4_p14[5], dip_7408_4_p15[5], dip_7486_8_p11[4], dip_7486_1_p5[4], dip_7486_6_p14[4]
  // DIP_7408 dip_7408_3: pin names not known; wires that end beside it: dip_7486_4_p15[4], dip_7408_4_p14[4], dip_7408_4_p15[4], dip_7486_8_p11[3], dip_7486_1_p5[3], dip_7486_6_p14[3], dip_7486_4_p15[3], dip_7408_4_p14[3], dip_7408_4_p15[3], dip_7486_8_p11[2], dip_7486_1_p5[2], dip_7486_6_p14[2]
  // DIP_7486 dip_7486_7: pin names not known; wires that end beside it: dip_7486_8_p11[7], dip_7486_8_p11[3], dip_7486_6_p14[7], dip_7486_6_p14[3], SUMME[7], SUMME[3], dip_7486_8_p11[6], dip_7486_8_p11[2], dip_7486_6_p14[6]
  // DIP_7486 dip_7486_8: pin names not known; wires that end beside it: dip_7486_6_p14[2], SUMME[6], SUMME[2], dip_7486_8_p11[5], dip_7486_8_p11[1], dip_7486_6_p14[5], dip_7486_6_p14[1], SUMME[5], SUMME[1], dip_7486_8_p11[4], dip_7486_8_p11[0], dip_7486_6_p14[4], dip_7486_6_p14[0], SUMME[4], SUMME[0]
  // DIP_7408 dip_7408_4: pin names not known; wires that end beside it: dip_7486_4_p15[2], dip_7408_4_p14[2], dip_7408_4_p15[2], dip_7486_8_p11[1], dip_7486_1_p5[1], dip_7486_6_p14[1], dip_7486_4_p15[1], dip_7408_4_p14[1], dip_7408_4_p15[1], dip_7486_8_p11[0], dip_7486_1_p5[0], dip_7486_6_p14[0], dip_7486_4_p15[0], dip_7408_4_p14[0], dip_7408_4_p15[0]
  // DIP_7486 dip_7486_9: pin names not known; wires that end beside it: dip_7408_4_p14[7], dip_7408_4_p14[3], dip_7408_4_p15[7], dip_7408_4_p15[3], dip_7486_9_p5, dip_7486_8_p11[4], dip_7408_4_p14[6], dip_7408_4_p14[2], dip_7408_4_p15[6]
  // DIP_7486 dip_7486_10: pin names not known; wires that end beside it: SUB_B, SUB_A, dip_7486_8_p11[0], SUB_B, dip_7486_9_p5, SUB_A, dip_7486_10_p7, dip_7486_10_p7, CARRY
  // DIP_7486 dip_7486_11: pin names not known; wires that end beside it: dip_7408_4_p15[2], dip_7486_8_p11[7], dip_7486_8_p11[3], dip_7408_4_p14[5], dip_7408_4_p14[1], dip_7408_4_p15[5], dip_7408_4_p15[1], dip_7486_8_p11[6], dip_7486_8_p11[2], dip_7408_4_p14[4], dip_7408_4_p14[0], dip_7408_4_p15[4], dip_7408_4_p15[0], dip_7486_8_p11[5], dip_7486_8_p11[1]

  // Notes on the sheet:
  //   CARRY
endmodule

module SHL74 (
  input  [7:0] A,
  input  [7:0] B,
  output [7:0] Output_Acc
);

  wire dip_7404_1_p3, dip_7408_1_p3, dip_7408_1_p9, dip_7408_2_p6, dip_7408_2_p7, dip_7408_2_p12,
       dip_7408_2_p13, dip_7432_1_p3, dip_7432_1_p4, dip_7432_1_p5, dip_7432_1_p6, dip_74151_1_p5,
       dip_74151_2_p5;

  // DIP_7432 dip_7432_1: pin names not known; wires that end beside it: B[7], B[5], dip_7432_1_p3, dip_7432_1_p4, dip_7432_1_p5, dip_7432_1_p6, B[6], B[4], dip_7432_1_p6, B[3], dip_7432_1_p4
  // DIP_7404 dip_7404_1: pin names not known; wires that end beside it: dip_7432_1_p3, dip_7432_1_p5, dip_7404_1_p3
  // DIP_74151 dip_74151_1: pin names not known; wires that end beside it: 1'b0, 1'b0, 1'b0, A[0], dip_74151_1_p5, 1'b0, 1'b0, 1'b0, 1'b0, 1'b0, B[0], B[1], B[2]
  // DIP_7408 dip_7408_1: pin names not known; wires that end beside it: dip_7404_1_p3, dip_7404_1_p3, dip_7408_1_p3, dip_74151_1_p5, Output_Acc[4], Output_Acc[0], dip_7404_1_p3, dip_7404_1_p3, dip_7408_1_p9
  // DIP_74151 dip_74151_2: pin names not known; wires that end beside it: 1'b0, 1'b0, A[0], A[1], dip_74151_2_p5, 1'b0, 1'b0, 1'b0, 1'b0, 1'b0, B[0], B[1], B[2]
  // DIP_7408 dip_7408_2: pin names not known; wires that end beside it: dip_74151_2_p5, Output_Acc[5], Output_Acc[1], dip_7404_1_p3, dip_7404_1_p3, dip_7408_2_p6, dip_7408_2_p7, Output_Acc[6], Output_Acc[2], dip_7404_1_p3, dip_7404_1_p3, dip_7408_2_p12, dip_7408_2_p13, Output_Acc[7], Output_Acc[3]
  // DIP_74151 dip_74151_3: pin names not known; wires that end beside it: 1'b0, A[0], A[1], A[2], dip_7408_2_p7, 1'b0, 1'b0, 1'b0, 1'b0, 1'b0, B[0], B[1], B[2]
  // DIP_74151 dip_74151_4: pin names not known; wires that end beside it: A[0], A[1], A[2], A[3], dip_7408_2_p13, 1'b0, 1'b0, 1'b0, 1'b0, 1'b0, B[0], B[1], B[2]
  // DIP_74151 dip_74151_5: pin names not known; wires that end beside it: A[1], A[2], A[3], A[4], dip_7408_1_p3, 1'b0, A[0], 1'b0, 1'b0, 1'b0, B[0], B[1], B[2]
  // DIP_74151 dip_74151_6: pin names not known; wires that end beside it: A[2], A[3], A[4], A[5], dip_7408_1_p9, 1'b0, A[1], A[0], 1'b0, 1'b0, B[0], B[1], B[2]
  // DIP_74151 dip_74151_7: pin names not known; wires that end beside it: A[3], A[4], A[5], A[6], dip_7408_2_p6, 1'b0, A[2], A[1], A[0], 1'b0, B[0], B[1], B[2]
  // DIP_74151 dip_74151_8: pin names not known; wires that end beside it: A[4], A[5], A[6], A[7], dip_7408_2_p12, 1'b0, A[3], A[2], A[1], A[0], B[0], B[1], B[2]
endmodule

module SHR74 (
  input  [7:0] A,
  input  [7:0] B,
  output [7:0] Output_Acc
);

  wire dip_7404_1_p3, dip_7408_1_p3, dip_7408_1_p9, dip_7408_2_p6, dip_7408_2_p7, dip_7408_2_p12,
       dip_7408_2_p13, dip_7432_1_p3, dip_7432_1_p4, dip_7432_1_p5, dip_7432_1_p6, dip_74151_1_p5,
       dip_74151_2_p5;

  // DIP_7432 dip_7432_1: pin names not known; wires that end beside it: B[7], B[5], dip_7432_1_p3, dip_7432_1_p4, dip_7432_1_p5, dip_7432_1_p6, B[6], B[4], dip_7432_1_p6, B[3], dip_7432_1_p4
  // DIP_7404 dip_7404_1: pin names not known; wires that end beside it: dip_7432_1_p3, dip_7432_1_p5, dip_7404_1_p3
  // DIP_74151 dip_74151_1: pin names not known; wires that end beside it: 1'b0, 1'b0, 1'b0, A[7], dip_74151_1_p5, 1'b0, 1'b0, 1'b0, 1'b0, 1'b0, B[0], B[1], B[2]
  // DIP_7408 dip_7408_1: pin names not known; wires that end beside it: dip_7404_1_p3, dip_7404_1_p3, dip_7408_1_p3, dip_74151_1_p5, Output_Acc[3], Output_Acc[7], dip_7404_1_p3, dip_7404_1_p3, dip_7408_1_p9
  // DIP_74151 dip_74151_2: pin names not known; wires that end beside it: 1'b0, 1'b0, A[7], A[6], dip_74151_2_p5, 1'b0, 1'b0, 1'b0, 1'b0, 1'b0, B[0], B[1], B[2]
  // DIP_7408 dip_7408_2: pin names not known; wires that end beside it: dip_74151_2_p5, Output_Acc[2], Output_Acc[6], dip_7404_1_p3, dip_7404_1_p3, dip_7408_2_p6, dip_7408_2_p7, Output_Acc[1], Output_Acc[5], dip_7404_1_p3, dip_7404_1_p3, dip_7408_2_p12, dip_7408_2_p13, Output_Acc[0], Output_Acc[4]
  // DIP_74151 dip_74151_3: pin names not known; wires that end beside it: 1'b0, A[7], A[6], A[5], dip_7408_2_p7, 1'b0, 1'b0, 1'b0, 1'b0, 1'b0, B[0], B[1], B[2]
  // DIP_74151 dip_74151_4: pin names not known; wires that end beside it: A[7], A[6], A[5], A[4], dip_7408_2_p13, 1'b0, 1'b0, 1'b0, 1'b0, 1'b0, B[0], B[1], B[2]
  // DIP_74151 dip_74151_5: pin names not known; wires that end beside it: A[6], A[5], A[4], A[3], dip_7408_1_p3, 1'b0, A[7], 1'b0, 1'b0, 1'b0, B[0], B[1], B[2]
  // DIP_74151 dip_74151_6: pin names not known; wires that end beside it: A[5], A[4], A[3], A[2], dip_7408_1_p9, 1'b0, A[6], A[7], 1'b0, 1'b0, B[0], B[1], B[2]
  // DIP_74151 dip_74151_7: pin names not known; wires that end beside it: A[4], A[3], A[2], A[1], dip_7408_2_p6, 1'b0, A[5], A[6], A[7], 1'b0, B[0], B[1], B[2]
  // DIP_74151 dip_74151_8: pin names not known; wires that end beside it: A[3], A[2], A[1], A[0], dip_7408_2_p12, 1'b0, A[4], A[5], A[6], A[7], B[0], B[1], B[2]
endmodule

module INV74 (
  input  [7:0] Input,
  input  INV,
  output [7:0] Output
);

  wire [7:0] bit_extender_1_out;

  assign bit_extender_1_out = {{7{INV}}, INV};  // Bit_Extender bit_extender_1
  // DIP_7486 dip_7486_1: pin names not known; wires that end beside it: bit_extender_1_out[7], bit_extender_1_out[4], Input[7], Input[3], Output[7], Output[3], bit_extender_1_out[6], bit_extender_1_out[5], Input[6], Input[2], Output[6], Output[2]
  // DIP_7486 dip_7486_2: pin names not known; wires that end beside it: bit_extender_1_out[1], bit_extender_1_out[2], Input[5], Input[1], Output[5], Output[1], bit_extender_1_out[0], bit_extender_1_out[3], Input[4], Input[0], Output[4], Output[0]
endmodule

module CMPZERO74 (
  input  [7:0] Input,
  output is_zero
);

  wire dip_7432_1_p3, dip_7432_1_p4, dip_7432_1_p5, dip_7432_1_p10, dip_7432_1_p11, dip_7432_2_p5,
       dip_7432_2_p6;

  // DIP_7432 dip_7432_1: pin names not known; wires that end beside it: Input[5], Input[4], dip_7432_1_p3, dip_7432_1_p4, dip_7432_1_p5, dip_7432_1_p3, dip_7432_1_p5, Input[3], Input[6], dip_7432_1_p10, dip_7432_1_p11
  // DIP_7432 dip_7432_2: pin names not known; wires that end beside it: dip_7432_1_p4, dip_7432_1_p11, Input[2], Input[7], dip_7432_2_p5, dip_7432_2_p6, dip_7432_1_p10, Input[1]
  // DIP_7404 dip_7404_1: pin names not known; wires that end beside it: Input[0], dip_7432_2_p5, dip_7432_2_p6, is_zero
endmodule

module MUX (
  input  [7:0] ADD,
  input  [2:0] CU,
  input  [7:0] SUB,
  input  [7:0] AND,
  input  [7:0] OR,
  input  [7:0] XOR,
  input  [7:0] SHL,
  input  [7:0] SHR,
  input  [7:0] A,
  output [7:0] Output_Accu
);

  Mux2bit MUX_Modul (
    ._8_Bit_input_1({A[0], SHR[0], SHL[0], XOR[0], OR[0], AND[0], SUB[0], ADD[0]}), .Bit_2(Output_Accu[1]),
    .Bit_1(Output_Accu[0]), .CU(CU),
    ._8_Bit_input_1_2({A[1], SHR[1], SHL[1], XOR[1], OR[1], AND[1], SUB[1], ADD[1]}));
  Mux2bit MUX_Modul_2 (
    ._8_Bit_input_1({A[2], SHR[2], SHL[2], XOR[2], OR[2], AND[2], SUB[2], ADD[2]}), .Bit_2(Output_Accu[3]),
    .Bit_1(Output_Accu[2]), .CU(CU),
    ._8_Bit_input_1_2({A[3], SHR[3], SHL[3], XOR[3], OR[3], AND[3], SUB[3], ADD[3]}));
  Mux2bit MUX_Modul_3 (
    ._8_Bit_input_1({A[4], SHR[4], SHL[4], XOR[4], OR[4], AND[4], SUB[4], ADD[4]}), .Bit_2(Output_Accu[5]),
    .Bit_1(Output_Accu[4]), .CU(CU),
    ._8_Bit_input_1_2({A[5], SHR[5], SHL[5], XOR[5], OR[5], AND[5], SUB[5], ADD[5]}));
  Mux2bit MUX_Modul_4 (
    ._8_Bit_input_1({A[6], SHR[6], SHL[6], XOR[6], OR[6], AND[6], SUB[6], ADD[6]}), .Bit_2(Output_Accu[7]),
    .Bit_1(Output_Accu[6]), .CU(CU),
    ._8_Bit_input_1_2({A[7], SHR[7], SHL[7], XOR[7], OR[7], AND[7], SUB[7], ADD[7]}));
endmodule

module Mux2bit (
  input  [2:0] CU,
  input  [7:0] _8_Bit_input_1,
  input  [7:0] _8_Bit_input_1_2,
  output Bit_1,
  output Bit_2
);

  // DIP_74151 dip_74151_1: pin names not known; wires that end beside it: _8_Bit_input_1[3], _8_Bit_input_1[2], _8_Bit_input_1[1], _8_Bit_input_1[0], Bit_1, 1'b0, _8_Bit_input_1[4], _8_Bit_input_1[5], _8_Bit_input_1[6], _8_Bit_input_1[7], CU[0], CU[1], CU[2]
  // DIP_74151 dip_74151_2: pin names not known; wires that end beside it: _8_Bit_input_1_2[3], _8_Bit_input_1_2[2], _8_Bit_input_1_2[1], _8_Bit_input_1_2[0], Bit_2, 1'b0, _8_Bit_input_1_2[4], _8_Bit_input_1_2[5], _8_Bit_input_1_2[6], _8_Bit_input_1_2[7], CU[0], CU[1], CU[2]
endmodule

module test (
  input  in_1,
  input  in_2,
  input  in_3,
  input  in_4,
  input  in_5,
  input  in_6,
  input  in_7
);

  wire dip_74153_1_p1;

  // DIP_74153 dip_74153_1: pin names not known; wires that end beside it: dip_74153_1_p1, in_2, in_7, in_4, in_5, in_3, in_6, dip_74153_1_p1, in_2, in_1
endmodule

// 74125
module DIP_74125 (
  input  A1,
  input  C1,
  input  A2,
  input  C2,
  input  A3,
  input  C3,
  input  A4,
  input  C4,
  output Y1,
  output Y2,
  output Y3,
  output Y4
);

  wire not_1_out, not_2_out, not_3_out, not_4_out;

  assign Y1 = not_1_out ? A1 : 1'bz;  // Controlled_Buffer controlled_buffer_1
  not not_1 (not_1_out, C1);
  assign Y2 = not_2_out ? A2 : 1'bz;  // Controlled_Buffer controlled_buffer_2
  not not_2 (not_2_out, C2);
  assign Y3 = not_3_out ? A3 : 1'bz;  // Controlled_Buffer controlled_buffer_3
  not not_3 (not_3_out, C3);
  assign Y4 = not_4_out ? A4 : 1'bz;  // Controlled_Buffer controlled_buffer_4
  not not_4 (not_4_out, C4);
endmodule

// CBuf
module Tri_State_Buffer (
  input  [7:0] Input,
  input  NotActive,
  output [7:0] Output
);

  DIP_74125 dip_74125_1 (
    .A1(Input[0]), .C1(NotActive), .A2(Input[1]), .C2(NotActive), .A3(Input[3]), .C3(NotActive),
    .A4(Input[2]), .C4(NotActive), .Y1(Output[0]), .Y2(Output[1]), .Y3(Output[3]), .Y4(Output[2]));
  DIP_74125 dip_74125_2 (
    .A1(Input[4]), .C1(NotActive), .A2(Input[5]), .C2(NotActive), .A3(Input[7]), .C3(NotActive),
    .A4(Input[6]), .C4(NotActive), .Y1(Output[4]), .Y2(Output[5]), .Y3(Output[7]), .Y4(Output[6]));
endmodule

module RegisterUpdateSelection (
);

  Tri_State_Buffer tri_state_buffer_1 ();  // open: Input, NotActive, Output
endmodule
